# Fritzing sketch Smartgarden1 (saved by Fritzing 1.0.1rc)

parts:
  DS3231_RTC_Echtzeituhr = ZS-042 RTC Module
  4-Kanal-Relais = 2 channel relay module [package=THT]
  Raspberry_Pi_4B = Raspberry Pi 4B  # not connected
  Kapazitiver_Bodenfeuchtigkeitssensor_v2_0 = DFRobot Capacitive Soil Moisture Sensor V1.0 [part_number=SEN0193]
  Wasserpumpe = water pump/motor
  ESP8266_mit_Protoshield = ESP8266 NodeMCU LoLin base
  LCD_Display = LCD screen
  LCM1602_IIC1 = LCM1602 IIC [part_number="LCM1602 IIC" chip_label="LCM1602 IIC" package="DIP (Dual Inline) [THT]"]
  JSN_Ultraschallsensor = JSN-SRO4T [package=THT]

nets:
  GND: DS3231_RTC_Echtzeituhr.GND, Wasserpumpe.pin_1, ESP8266_mit_Protoshield.GND3-0, ESP8266_mit_Protoshield.GND3-2, ESP8266_mit_Protoshield.GND8-0, LCM1602_IIC1.GND
  VCC: DS3231_RTC_Echtzeituhr.VCC, 4-Kanal-Relais.Pin_25, Kapazitiver_Bodenfeuchtigkeitssensor_v2_0.VCC, ESP8266_mit_Protoshield.3V3-0, ESP8266_mit_Protoshield.3V3-1, ESP8266_mit_Protoshield.3V3-2, LCM1602_IIC1.VCC
  N1: DS3231_RTC_Echtzeituhr.SDA, ESP8266_mit_Protoshield.D2-0, ESP8266_mit_Protoshield.D2-2
  N2: DS3231_RTC_Echtzeituhr.SCL, ESP8266_mit_Protoshield.D1-0, ESP8266_mit_Protoshield.D1-2
  N3: 4-Kanal-Relais.Pin_10, Wasserpumpe.pin_2
  N4: 4-Kanal-Relais.Pin_11, ESP8266_mit_Protoshield.VUSB-0
  N5: 4-Kanal-Relais.Pin_27, ESP8266_mit_Protoshield.D5-0, ESP8266_mit_Protoshield.D5-2
  N6: 4-Kanal-Relais.Pin_28, ESP8266_mit_Protoshield.D6-0, ESP8266_mit_Protoshield.D6-2
  N7: Kapazitiver_Bodenfeuchtigkeitssensor_v2_0.A, ESP8266_mit_Protoshield.A0
  N8: ESP8266_mit_Protoshield.D4-0, JSN_Ultraschallsensor.pin3
  N9: ESP8266_mit_Protoshield.D7-0, JSN_Ultraschallsensor.pin2
  VSS: LCD_Display.VSS, LCM1602_IIC1.VSS
  VDD: LCD_Display.VDD, LCM1602_IIC1.VDD
  N10: LCD_Display.V0, LCM1602_IIC1.V0
  N11: LCD_Display.RS, LCM1602_IIC1.RS
  N12: LCD_Display.R/W, LCM1602_IIC1.RW
  N13: LCD_Display.E, LCM1602_IIC1.E
  N14: LCD_Display.DB0, LCM1602_IIC1.D0
  N15: LCD_Display.DB1, LCM1602_IIC1.D1
  N16: LCD_Display.DB2, LCM1602_IIC1.D2
  N17: LCD_Display.DB3, LCM1602_IIC1.D3
  N18: LCD_Display.DB4, LCM1602_IIC1.D4
  N19: LCD_Display.DB5, LCM1602_IIC1.D5
  N20: LCD_Display.DB6, LCM1602_IIC1.D6
  N21: LCD_Display.DB7, LCM1602_IIC1.D7
  N22: LCD_Display.LED+, LCM1602_IIC1.A
  N23: LCD_Display.LED-, LCM1602_IIC1.K

notes:
  Pflanzenlicht
  230 VAC

custom parts:
  2 channel relay module: 4 channel Relay Module 5V 12V 24V High and Low Level Trigger Relay Control With Optocoupler Two Way relays DC 5 V 12 V 24 V Volt.
  DFRobot Capacitive Soil Moisture Sensor V1.0: DFRobot Capacitive Soil Moisture Sensor V1.0 This product measures soil moisture levels by capacitive sensing, rather than resistive sensing like other types of moisture sensor. It is made of a corrosion resistant material giving it a long service life. Insert it into soil and impress your friends with the real-time soil moisture data! The product includes an on-board voltage regulator which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
  water pump/motor: WATER PUMP BY ARDUBLOCKTR
  ESP8266 NodeMCU LoLin base: ESP8266 based NodeMCU Base
  LCM1602 IIC: I2C-Module to use a 1602 or 2004 LCD on with the wire.h libory Serial LCD Modul
  JSN-SRO4T: JSN-SR04T Waterproof Ultrasonic Distance Measuring Module Integrated Ultrasonic Detection Module DC 5V.

// code stored in the sketch: Smartgarden2.ino
/*
    /////////////////////////////////////////////////////////////
   //                                                         //
  //                    Smartgarden                          //
 //                                                         //
/////////////////////////////////////////////////////////////
 */

/*===============================================================
Descprition: Diplomarbeit Smartgarden mit MQTT
Author     : Dieudonné de Oliveira
Date       : 12.02.2024
Version    : V05.00.00
===============================================================*/

#include <Wire.h>
#include <LiquidCrystal_I2C.h>
#include <ESP8266WiFi.h>
#include <PubSubClient.h>
#include <RTClib.h>

#define ssid "FibreBox_X6-0E6AC7"
#define password "YCX7JATHRQRMYNPURM"
#define mqtt_server "192.168.1.19"

#define switch_topic "esp8266/switch"
#define status_topic "esp8266/status" 
#define inTopic "esp8266/output"
#define outTopic "esp8266/sensor"

const int soilMoisturePin = A0;
const int lightRelay = D5; // Pin für das Relais der Pflanzenbeleuchtung
const int pumpRelay = D6;  // Pin für das Relais der Wasserpumpe
const int trigPin = D4;    // Pin für den Ultraschallsensor (Trig)
const int echoPin = D7;    // Pin für den Ultraschallsensor (Echo)

//int soilMoistureOffset = 695; // Korrekturwert für die Bodenfeuchte
int SoilMoisturepercentage;   // Variable für Bodenfeuchte
int counter = 0;  // Counter für die Case-Anweisung


WiFiClient espClient;
PubSubClient client(espClient);
RTC_DS3231 rtc; // Real Time Clock definieren
LiquidCrystal_I2C lcd = LiquidCrystal_I2C(0x27, 16, 2); // LCD definieren D1 und D2

void setup() {
  Serial.begin(9600);
  setup_wifi();
  client.setServer(mqtt_server, 1884); // MQTT Server und Port
  setup_rtc();
  client.setCallback(callback);
  lcd.init(); // LCD initialisieren
  lcd.backlight();  // Hintergrundbeleuchtung einschalten
  pinMode(soilMoisturePin, INPUT);
  pinMode(lightRelay, OUTPUT);
  pinMode(pumpRelay, OUTPUT);
  pinMode(trigPin, OUTPUT);
  pinMode(echoPin, INPUT);
  digitalWrite(lightRelay, LOW);
  digitalWrite(pumpRelay, HIGH);
}

void loop() {
  if (!client.connected()) {
    reconnect();
  }
  client.loop();

  // Überprüfung der Counter-Werte für die verschiedenen Aktionen
  switch(counter) {
    case 5:
      soilMoisture();
      break;
    case 10:
      check_waterlevel();
      break;
    case 15:
      light();
      break;
    case 20:
      pump();
      break;  
    default:
      delay(1000); // Warten, bevor die Schleife erneut durchlaufen wird
      break;
  }

  // Inkrementieren des Zählers
  counter++;

  // Zurücksetzen des Zählers, wenn er die maximale Anzahl erreicht hat
  if (counter > 20) {
    counter = 0;
  }
}


// Wifi initialisieren
void setup_wifi() {
  delay(10);
  Serial.println();
  Serial.print("Connecting to ");
  Serial.println(ssid);
  WiFi.begin(ssid, password);
  while (WiFi.status() != WL_CONNECTED) {
    Serial.print(".");
    delay(500);
  }
  Serial.println("");
  Serial.println("WiFi connected");
  Serial.println("IP address: ");
  Serial.println(WiFi.localIP());
}
void callback(char* topic, byte* message, unsigned int length) {
  Serial.print("Message arrived on topic: ");
  Serial.print(topic);
  Serial.print(". Message: ");
  String messageTemp;
  
  for (int i = 0; i < length; i++) {
    Serial.print((char)message[i]);
    messageTemp += (char)message[i];
  }
  
  Serial.println();

  if (String(topic) == "esp8266/output") {
    Serial.print("Changing output to ");
    if(messageTemp == "true"){
      Serial.println("on");
      digitalWrite(pumpRelay, LOW);
      client.publish(switch_topic, "ON");
      delay(200);
    }
    else if(messageTemp == "false"){
      Serial.println("off");
      digitalWrite(pumpRelay, HIGH);  
      client.publish(switch_topic, "OFF");
      delay(200);
    }
  }
}
// Verbindung mit dem MQTT und dem ESP8266
// Meldungen im seriellen Monitor und auf NodeRed
void reconnect() {
  while (!client.connected()) {
    Serial.print("Attempting MQTT connection...");
    if (client.connect("SmartGardenClient")) {
      Serial.println("connected");
      client.publish(status_topic, "Er lebt");
      client.subscribe(inTopic);
    } 
    else {
      Serial.print("failed, rc=");
      Serial.print(client.state());
      Serial.println(" try again in 5 seconds");
      delay(5000);
    }
  }
}

// Real Time Clock aufsetzen
void setup_rtc() {
  if (!rtc.begin()) {
    Serial.println("Couldn't find RTC");
    while (1);
  }
  if (rtc.lostPower()) {
    Serial.println("RTC lost power, let's set the time!");
    rtc.adjust(DateTime(F(__DATE__), F(__TIME__)));
  }
}

// Bodenfeuchte prüfen
void soilMoisture() {
  int sensorValue = analogRead(soilMoisturePin);
  
  // Korrigierten Bodenfeuchte-Wert berechnen
  //int correctedSoilMoistureValue = sensorValue - soilMoistureOffset;

  // Den Wert auf den Bereich von 0 bis 100 Prozent abbilden
  int percentageSoilMoisture = map(sensorValue, 495, 696, 100, 0);

  // Wert an Node-RED senden
  client.publish(outTopic, String(percentageSoilMoisture).c_str());
  char gauge [10]; // Sending percentage value to NodeRed need char array 
  itoa(percentageSoilMoisture,gauge,10); // Change int value to char array
  client.publish(outTopic, gauge); // Send value to NodeRed
  delay(500); // Wait 0.5 seconds
  // Wert als globale Variable aktualisieren
  SoilMoisturepercentage = percentageSoilMoisture;



  delay(500);
}

void check_waterlevel() {
    digitalWrite(trigPin, LOW);
    delayMicroseconds(2);
    digitalWrite(trigPin, HIGH);
    delayMicroseconds(10);
    digitalWrite(trigPin, LOW);
    long duration = pulseIn(echoPin, HIGH);
    float distance = (duration / 2) * 0.0343;
    float waterLevel = 10 - distance; // Hier Wert für maximale Wassertiefe einfügen
    if (waterLevel < 0) waterLevel = 0; // Sicherstellen, dass der Wert nicht negativ wird
    Serial.print("Distance: ");
  Serial.print(distance);
  Serial.println(" cm");
    // Wasserstand an Node-RED senden
    client.publish("garden/water", String(waterLevel).c_str());
    if (waterLevel < 10) {
      client.publish("garden/water", "Niedriger Pegel, nachfüllen");
      lcd.clear(); 
    lcd.setCursor(0,0); 
    lcd.print("Wasserstand"); 
    lcd.setCursor(0,1); 
    lcd.print("niedrig");
    }
    //return waterLevel;
}

void light() {
  DateTime now = rtc.now();
  int currentHour = now.hour();

  if (currentHour >= 18 || currentHour < 6) {
    digitalWrite(lightRelay, HIGH);
  } else {
    digitalWrite(lightRelay, LOW);
  }
}

void pump() {
  if (SoilMoisturepercentage >= 50) {
    lcd.clear(); 
    lcd.setCursor(0,0); 
    lcd.print("Bodenfeuchte"); 
    lcd.setCursor(0,1); 
    lcd.print("optimal");
    Serial.println("Stop");
  } else if (SoilMoisturepercentage <= 49 && SoilMoisturepercentage >=30) {
    lcd.clear(); 
    lcd.setCursor(0,0); 
    lcd.print("Bodenfeuchte"); 
    lcd.setCursor(0,1); 
    lcd.print("genug");
    Serial.println("Genug");
  } else if (SoilMoisturepercentage < 30) {
    lcd.clear(); 
    lcd.setCursor(0,0); 
    lcd.print("Bodenfeuchte"); 
    lcd.setCursor(0,1); 
    lcd.print("zu trocken"); 
    delay(1000); 
    lcd.clear(); 
    lcd.setCursor(0,0); 
    lcd.print("Wasserpumpe"); 
    lcd.setCursor(0,1); 
    lcd.print("an"); 
    digitalWrite(pumpRelay, LOW); 
    delay(10000); 
    digitalWrite(pumpRelay, HIGH); 
    lcd.clear(); 
    lcd.setCursor(0,0); 
    lcd.print("Wasserpumpe"); 
    lcd.setCursor(0,1); 
    lcd.print("aus");
    Serial.println("Ich bin durstig"); 
    delay(10000); 
  }
}
